# Fritzing sketch DRIVER_STEPPER (saved by Fritzing 0.9.3b)
circuit board: 4.2cm x 6cm
breadboards: 1

parts:
  DRV_3 = DRV 8825 Stepper Motor Carrier, High Current [part_number="DRV 8825"]
  DRV_4 = DRV 8825 Stepper Motor Carrier, High Current [part_number="DRV 8825"]
  J7 = molex pin header, 4 pins [form=molex]
  J8 = molex pin header, 4 pins [form=molex]
  C3 = Electrolytic Capacitor [capacitance=0.1mF package="100 mil [THT, electrolytic]"]
  C4 = Electrolytic Capacitor [capacitance=0.1mF package="100 mil [THT, electrolytic]"]
  LED2 = LED - 5mm [color="Red (633nm)" package="5 mm [THT]"]
  R2 = Resistor [tolerance=±5% resistance=1k package=THT]
  F4 = Resettable Fuse PTC [package=ptc]
  ENC_3 = molex pin header, 4 pins [form=molex]
  ENC_4 = molex pin header, 4 pins [form=molex]
  J12 = double row female pin header, 10 pins [form="♀ (female)"]
  IC1 = IC, DIP package, 6 pins [chip_label=IC]
  J21 = molex pin header, 2 pins [form=molex]

nets:
  ENA_DROIT: DRV_3.ENABLE
  MS1_DROIT/MS1_GAUCHE: DRV_3.MS1, DRV_4.MS1, IC1.pin3
  MS2_DROIT/MS2_GAUCHE: DRV_3.MS2, DRV_4.MS2, IC1.pin2
  MS3_DROIT/MS3_GAUCHE: DRV_3.MS3, DRV_4.MS3, IC1.pin1
  5V: DRV_3.RESET, DRV_3.SLEEP, DRV_4.RESET, DRV_4.SLEEP, ENC_3.pin3, ENC_4.pin3, J12.pin1, IC1.pin4, IC1.pin5, IC1.pin6
  D6/STEP_DROIT: DRV_3.STEP, J12.pin8
  D7/DIR_DROIT: DRV_3.DIRECTION, J12.pin7
  12V: DRV_3.VOLTAGE_ST/_MT, DRV_4.VOLTAGE_ST/_MT, C3.+, C4.+, R2.Pin_0, F4.1
  GND: DRV_3.GROUND_ST/_MT, DRV_4.GROUND_ST/_MT, C3.-, C4.-, LED2.cathode, J21.pin1
  N1: DRV_3.OUT_2B, J7.pin1
  N2: DRV_3.OUT_2A, J7.pin2
  N3: DRV_3.OUT_1A, J7.pin3
  N4: DRV_3.OUT_1B, J7.pin4
  GND2: DRV_3.GROUND_LOG, DRV_4.GROUND_LOG, ENC_3.pin4, ENC_4.pin4, J12.pin10
  ENA_GAUCHE: DRV_4.ENABLE
  D5/STEP_GAUCHE: DRV_4.STEP, J12.pin9
  D8/DIR_GAUCHE: DRV_4.DIRECTION, J12.pin6
  N5: DRV_4.OUT_2B, J8.pin1
  N6: DRV_4.OUT_2A, J8.pin2
  N7: DRV_4.OUT_1A, J8.pin3
  N8: DRV_4.OUT_1B, J8.pin4
  N9: LED2.anode, R2.Pin_1
  N10: F4.2, J21.pin2
  D12/GAUCHE_CHA: ENC_3.pin1, J12.pin2
  D11/GAUCHE_CHB: ENC_3.pin2, J12.pin3
  D10/DROITE_CHA: ENC_4.pin1, J12.pin4
  D9/DROITE_CHB: ENC_4.pin2, J12.pin5

notes:
  Karibous 2017, A
  +
  -
  Driver
  Pas-à-pas
