# Fritzing sketch INTERFACE (saved by Fritzing 0.9.3b)
circuit board: 4.2cm x 5.99877cm
breadboards: 1

parts:
  J11 = double row female pin header, 10 pins [form="♀ (female)"]
  J12 = molex pin header, 3 pins [form=molex]
  J13 = molex pin header, 3 pins [form=molex]
  J14 = molex pin header, 3 pins [form=molex]
  J15 = molex pin header, 3 pins [form=molex]
  J16 = molex pin header, 3 pins [form=molex]
  J17 = molex pin header, 3 pins [form=molex]
  J18 = molex pin header, 3 pins [form=molex]
  J19 = molex pin header, 3 pins [form=molex]
  R1 = Resistor [tolerance=±5% resistance=220 package=THT]
  LED1 = LED - 3mm [color="Red (633nm)" package="3 mm [THT]"]
  J20 = molex pin header, 2 pins [form=molex]
  D2 = Rectifier Diode [part_number=1N4007 package="300 mil [THT]"]
  F2 = Resettable Fuse PTC [package=ptc]
  R2 = Resistor [tolerance=±5% resistance=220 package=THT]
  LED2 = LED - 3mm [color="Red (633nm)" package="3 mm [THT]"]
  C1 = Electrolytic Capacitor [capacitance=0.47mF voltage=20V package="200 mil [THT, electrolytic]"]
  C2 = Electrolytic Capacitor [capacitance=0.47mF voltage=20V package="200 mil [THT, electrolytic]"]
  D24V50F5 = longpad pin header, 5 pins [form="long pad"]
  Pad1 = Pad [width=21.731111111111108 height=4.0922222222222224 connect=center]

nets:
  5V: J11.pin1
  A9: J11.pin2, J12.pin1
  A8: J11.pin3, J13.pin1
  A7: J11.pin4, J14.pin1
  A6: J11.pin5, J15.pin1
  A3: J11.pin6, J16.pin1
  A2: J11.pin7, J17.pin1
  A1: J11.pin8, J18.pin1
  A0: J11.pin9, J19.pin1
  GND: J11.pin10, J12.pin3, J13.pin3, J14.pin3, J15.pin3, J16.pin3, J17.pin3, J18.pin3, J19.pin3, LED1.cathode, J20.pin1, LED2.cathode, C1.-, C2.-, D24V50F5.pin2, D24V50F5.pin3
  VDD: J12.pin2, J13.pin2, J14.pin2, J15.pin2, J16.pin2, J17.pin2, J18.pin2, J19.pin2, R1.Pin_0, C1.+, C2.+, D24V50F5.pin1, Pad1.pad
  N1: R1.Pin_1, LED1.anode
  N2: J20.pin2, F2.1
  12V: D2.cathode, R2.Pin_0, D24V50F5.pin4
  N3: D2.anode, F2.2
  N4: R2.Pin_1, LED2.anode

notes:
  Carte d'interface
