# Fritzing sketch PUISSANCE_V4 (saved by Fritzing 0.9.3b)
circuit board: 6cm x 4.22cm
breadboards: 1

parts:
  J21 = molex pin header, 2 pins [form=molex]
  R1 = Resistor [tolerance=±5% resistance=220 package=THT]
  J22 = molex pin header, 2 pins [form=molex]
  J23 = molex pin header, 2 pins [form=molex]
  J24 = molex pin header, 2 pins [form=molex]
  J25 = molex pin header, 2 pins [form=molex]
  J26 = molex pin header, 2 pins [form=molex]
  J27 = molex pin header, 2 pins [form=molex]
  J28 = molex pin header, 2 pins [form=molex]
  J29 = molex pin header, 2 pins [form=molex]
  J30 = molex pin header, 2 pins [form=molex]
  J31 = molex pin header, 2 pins [form=molex]
  J32 = molex pin header, 2 pins [form=molex]
  J33 = screw terminal, 2 pins
  LED1 = LED - 3mm [color="Red (633nm)" package="3 mm [THT]"]
  Pad1 = Pad [width=46.624948928346875 height=24.988654192086717 connect=center]

nets:
  GND: J21.pin1, J22.pin1, J23.pin1, J24.pin1, J25.pin1, J26.pin1, J27.pin1, J28.pin1, J29.pin1, J30.pin1, J31.pin1, J32.pin1, J33.pin1, LED1.cathode
  VDD: J21.pin2, R1.Pin_0, J22.pin2, J23.pin2, J24.pin2, J25.pin2, J26.pin2, J27.pin2, J28.pin2, J29.pin2, J30.pin2, J31.pin2, J32.pin2, J33.pin2, Pad1.pad
  N1: R1.Pin_1, LED1.anode

notes:
  Les Karibous
  Carte Puissance 2017
  +
  -
