# Fritzing sketch TEENSY_3_2 (saved by Fritzing 0.9.3b)
circuit board: 6cm x 6cm
breadboards: 1

parts:
  J3 = molex pin header, 2 pins [form=molex]
  D1 = Rectifier Diode [part_number=1N4007 package="300 mil [THT]"]
  F1 = Resettable Fuse PTC [package=ptc]
  J4 = molex pin header, 4 pins [form=molex]
  R1 = Resistor [tolerance=±5% resistance=220 package=THT]
  R2 = Resistor [tolerance=±5% resistance=220 package=THT]
  J7 = molex pin header, 4 pins [form=molex]
  MCP2551 = IC, DIP package, 8 pins [chip_label=MCP2551]
  R5 = Resistor [tolerance=±5% resistance=120 package=THT]
  R6 = Resistor [tolerance=±5% resistance=10k package=THT]
  CAN = molex pin header, 3 pins [form=molex]
  SERIAL = molex pin header, 4 pins [form=molex]
  J9 = double row female pin header, 10 pins [form="♀ (female)"]
  J10 = double row female pin header, 10 pins [form="♀ (female)"]
  LED1 = LED - 3mm [color="Red (633nm)" package="3 mm [THT]"]
  LED2 = LED - 3mm [color="Green (570nm)" package="3 mm [THT]"]
  J6 = male pin header, 3 pins [form="♂ (male)"]
  SW1 = DIP SWITCH [package=dipswitch-02]
  R7 = Resistor [tolerance=±5% resistance=4.7k package=THT]
  R8 = Resistor [tolerance=±5% resistance=4.7k package=THT]
  D24V10F5 = longpad pin header, 5 pins [form="long pad"]
  Teensy_3_1 = Teensy 3.1

nets:
  GND/VDD: J3.pin1, J4.pin4, J7.pin4, MCP2551.pin3, R6.Pin_1, CAN.pin3, SERIAL.pin4, J9.pin10, J10.pin10, LED1.cathode, LED2.cathode, D24V10F5.pin4, Teensy_3_1.GND
  N1: J3.pin2, F1.1
  12V: D1.cathode, R1.Pin_0, D24V10F5.pin3
  N2: D1.anode, F1.2
  SDA1: J4.pin1, J7.pin1, SW1.1, Teensy_3_1.A4/D18
  SCL1: J4.pin2, J7.pin2, SW1.2, Teensy_3_1.A5/D19
  N3: J4.pin3, J7.pin3, J6.pin2
  N4: R1.Pin_1, LED1.anode
  5V/VSS: R2.Pin_0, MCP2551.pin2, SERIAL.pin3, J9.pin1, J10.pin1, D24V10F5.pin5, Teensy_3_1.Vin
  N5: R2.Pin_1, LED2.anode
  TXD: MCP2551.pin1, Teensy_3_1.D3
  RXD: MCP2551.pin4, Teensy_3_1.D4
  VREF: MCP2551.pin5
  CANL: MCP2551.pin6, R5.Pin_1, CAN.pin2
  CANH: MCP2551.pin7, R5.Pin_0, CAN.pin1
  RS: MCP2551.pin8, R6.Pin_0
  RXu: SERIAL.pin1, Teensy_3_1.D0
  TX: SERIAL.pin2, Teensy_3_1.D1
  D12: J9.pin2, Teensy_3_1.D12
  D11: J9.pin3, Teensy_3_1.D11
  D10: J9.pin4, Teensy_3_1.D10
  D9: J9.pin5, Teensy_3_1.D9
  D8: J9.pin6, Teensy_3_1.D8
  D7: J9.pin7, Teensy_3_1.D7
  D6: J9.pin8, Teensy_3_1.D6
  D5: J9.pin9, Teensy_3_1.D5
  A9: J10.pin2, Teensy_3_1.A9/D23
  A8: J10.pin3, Teensy_3_1.A8/D22
  A7: J10.pin4, Teensy_3_1.A7/D21
  A6: J10.pin5, Teensy_3_1.A6/D20
  A3: J10.pin6, Teensy_3_1.A3/D17
  A2: J10.pin7, Teensy_3_1.A2/D16
  A1: J10.pin8, Teensy_3_1.A1/D15
  A0: J10.pin9, Teensy_3_1.A0/D14
  3.3V: J6.pin3, R7.Pin_0, R8.Pin_0, Teensy_3_1.3V3
  N6: SW1.3, R8.Pin_1
  N7: SW1.4, R7.Pin_1
  D2: Teensy_3_1.D2
  NA1: Teensy_3_1.D13

notes:
  USB
